# Fritzing sketch HIH8120_PI (saved by Fritzing 0.9.3b)
breadboards: 1

parts:
  Raspberry_Pi_1 = Raspberry Pi 3 [part_number=RPI-3-V1.2]
  U1 = mystery part, 4 pins [chip_label=HIH8120 part_number=HIH8120]
  C1 = Ceramic Capacitor [capacitance=0.47mF package="100 mil [THT, multilayer]"]
  R1 = Resistor [tolerance=±5% resistance=2.2k package=THT]
  R2 = Resistor [tolerance=±5% resistance=2.2k package=THT]

nets:
  N1: Raspberry_Pi_1.3v3, U1.pin1, C1.0, R1.Pin_1, R2.Pin_1
  N2: Raspberry_Pi_1.GPIO2, U1.pin4, R2.Pin_0
  N3: Raspberry_Pi_1.GPIO3, U1.pin3, R1.Pin_0
  N4: Raspberry_Pi_1.GND, U1.pin2, C1.1
