# Fritzing sketch MCP23017 (saved by Fritzing 0.9.3b)
breadboards: 1

parts:
  Raspberry_Pi_1 = Raspberry Pi 3 [part_number=RPI-3-V1.2]
  U1 = IC, DIP package, 28 pins [chip_label=MCP23017]

nets:
  N1: Raspberry_Pi_1.GPIO2, U1.pin13
  N2: Raspberry_Pi_1.GPIO3, U1.pin12
  N3: Raspberry_Pi_1.GND, U1.pin10, U1.pin15, U1.pin16, U1.pin17, U1.pin18
  N4: Raspberry_Pi_1.5V, U1.pin9
